// Logisim project InstDecoder.circ as structural Verilog: 3 circuits, main circuit InstDecoder
module InstDecoder (
  input  [31:0] in_1,
  input  in_2,
  output [5:0] OpCode,
  output [25:0] JmpDest,
  output [5:0] FunCode,
  output [4:0] Rs,
  output [4:0] Rt,
  output out_8,
  output [4:0] Rd,
  output [15:0] Constant,
  output add,
  output sltu,
  output sub,
  output mfhi,
  output addi,
  output bne,
  output mul,
  output mflo,
  output andi,
  output blez,
  output mulu,
  output jr,
  output ori,
  output bgtz,
  output div,
  output nop,
  output xori,
  output bltz,
  output divu,
  output pop,
  output slti,
  output lw,
  output \and ,
  output push,
  output sluti,
  output sw,
  output \or ,
  output halt,
  output beq,
  output \nor ,
  output tty,
  output \xor ,
  output rnd,
  output slt,
  output kbp
);

  TypeR typer_1 (
    .in_1(in_1[31:26]), .in_2(in_1[5:0]), .add(add), .sub(sub), .mul(mul), .mulu(mulu), .div(div),
    .divu(divu), .\and (\and ), .\or (\or ), .\nor (\nor ), .\xor (\xor ), .slt(slt), .sltu(sltu),
    .mfhi(mfhi), .mfllo(mflo), .jr(jr), .nop(nop), .halt(halt), .tty(tty), .pop(pop), .push(push), .rnd(rnd),
    .kbp(kbp), .out_19(out_8));
  TypeI typei_1 (
    .in_1(in_1[31:26]), .addi(addi), .andi(andi), .ori(ori), .xori(xori), .slti(slti), .sltui(sluti),
    .beq(beq), .bne(bne), .blez(blez), .bgtz(bgtz), .bltz(bltz), .lw(lw), .sw(sw));  // open: addi_2

  assign Constant = in_1[15:0];
  assign FunCode = in_1[5:0];
  assign JmpDest = in_1[25:0];
  assign OpCode = in_1[31:26];
  assign Rd = in_1[15:11];
  assign Rs = in_1[25:21];
  assign Rt = in_1[20:16];

  // Other names for the same wires on the sheet: En = in_2; X[4:0] = in_1[10:6]; nTI_TR = out_8
endmodule

module TypeR (
  input  [5:0] in_1,
  input  [5:0] in_2,
  output add,
  output sub,
  output mul,
  output mulu,
  output div,
  output divu,
  output \and ,
  output \or ,
  output \nor ,
  output \xor ,
  output slt,
  output sltu,
  output mfhi,
  output mfllo,
  output jr,
  output nop,
  output out_19,
  output halt,
  output tty,
  output pop,
  output push,
  output rnd,
  output kbp
);

  wire R1, R2, R3;

  and and_1 (R1, ~in_1[0], ~in_1[1], ~in_1[2], ~in_1[3], ~in_1[4], ~in_1[5]);  // AND_Gate
  and and_2 (R2, ~in_1[0], ~in_1[1], ~in_1[2], in_1[3], in_1[4], in_1[5]);  // AND_Gate
  and and_3 (R3, in_1[0], in_1[1], in_1[2], in_1[3], in_1[4], in_1[5]);
  or or_1 (out_19, R1, R2, R3);
  and and_4 (add, ~in_2[0], ~in_2[1], ~in_2[2], ~in_2[3], ~in_2[4], in_2[5], R1);  // AND_Gate
  and and_5 (divu, in_2[0], in_2[1], ~in_2[2], in_2[3], in_2[4], ~in_2[5], R1);  // AND_Gate
  and and_6 (slt, ~in_2[0], in_2[1], ~in_2[2], in_2[3], ~in_2[4], in_2[5], R1);  // AND_Gate
  and and_7 (nop, ~in_2[0], ~in_2[1], ~in_2[2], ~in_2[3], ~in_2[4], ~in_2[5], R1);  // AND_Gate
  and and_8 (pop, ~in_2[0], ~in_2[1], ~in_2[2], ~in_2[3], ~in_2[4], ~in_2[5], R2);  // AND_Gate
  and and_9 (sub, ~in_2[0], in_2[1], ~in_2[2], ~in_2[3], ~in_2[4], in_2[5], R1);  // AND_Gate
  and and_10 (\and , ~in_2[0], ~in_2[1], in_2[2], ~in_2[3], ~in_2[4], in_2[5], R1);  // AND_Gate
  and and_11 (sltu, in_2[0], in_2[1], ~in_2[2], in_2[3], ~in_2[4], in_2[5], R1);  // AND_Gate
  and and_12 (push, in_2[0], ~in_2[1], ~in_2[2], ~in_2[3], ~in_2[4], ~in_2[5], R2);  // AND_Gate
  and and_13 (mul, ~in_2[0], ~in_2[1], ~in_2[2], in_2[3], in_2[4], ~in_2[5], R1);  // AND_Gate
  and and_14 (\or , in_2[0], ~in_2[1], in_2[2], ~in_2[3], ~in_2[4], in_2[5], R1);  // AND_Gate
  and and_15 (mfhi, ~in_2[0], ~in_2[1], ~in_2[2], ~in_2[3], in_2[4], ~in_2[5], R1);  // AND_Gate
  and and_16 (halt, in_2[0], in_2[1], in_2[2], in_2[3], in_2[4], in_2[5], R3);
  and and_17 (rnd, ~in_2[0], in_2[1], ~in_2[2], ~in_2[3], ~in_2[4], ~in_2[5], R3);  // AND_Gate
  and and_18 (mulu, in_2[0], ~in_2[1], ~in_2[2], in_2[3], in_2[4], ~in_2[5], R1);  // AND_Gate
  and and_19 (\nor , in_2[0], in_2[1], in_2[2], ~in_2[3], ~in_2[4], in_2[5], R1);  // AND_Gate
  and and_20 (mfllo, ~in_2[0], in_2[1], ~in_2[2], ~in_2[3], in_2[4], ~in_2[5], R1);  // AND_Gate
  and and_21 (div, ~in_2[0], in_2[1], ~in_2[2], in_2[3], in_2[4], ~in_2[5], R1);  // AND_Gate
  and and_22 (\xor , ~in_2[0], ~in_2[1], ~in_2[2], in_2[3], ~in_2[4], in_2[5], R1);  // AND_Gate
  and and_23 (jr, ~in_2[0], ~in_2[1], ~in_2[2], in_2[3], ~in_2[4], ~in_2[5], R1);  // AND_Gate
  and and_24 (tty, in_2[0], ~in_2[1], ~in_2[2], ~in_2[3], ~in_2[4], ~in_2[5], R3);  // AND_Gate
  and and_25 (kbp, ~in_2[0], ~in_2[1], in_2[2], ~in_2[3], ~in_2[4], ~in_2[5], R3);  // AND_Gate

  // Other names for the same wires on the sheet: FunCode[5:0] = in_2; OpCode[5:0] = in_1

  // Notes on the sheet:
  //   OPcode 111000
  //   OPcode 000000
  //   OPcode 111111
endmodule

module TypeI (
  input  [5:0] in_1,
  output addi,
  output andi,
  output ori,
  output xori,
  output slti,
  output sltui,
  output beq,
  output bne,
  output blez,
  output bgtz,
  output bltz,
  output lw,
  output sw,
  output addi_2
);

  and and_1 (addi, ~in_1[0], ~in_1[1], ~in_1[2], in_1[3], ~in_1[4], ~in_1[5]);  // AND_Gate
  and and_2 (sltui, in_1[0], in_1[1], ~in_1[2], in_1[3], ~in_1[4], ~in_1[5]);  // AND_Gate
  and and_3 (bltz, in_1[0], ~in_1[1], ~in_1[2], ~in_1[3], ~in_1[4], ~in_1[5]);  // AND_Gate
  and and_4 (andi, ~in_1[0], ~in_1[1], in_1[2], in_1[3], ~in_1[4], ~in_1[5]);  // AND_Gate
  and and_5 (beq, ~in_1[0], ~in_1[1], in_1[2], ~in_1[3], ~in_1[4], ~in_1[5]);  // AND_Gate
  and and_6 (lw, in_1[0], in_1[1], ~in_1[2], ~in_1[3], ~in_1[4], in_1[5]);  // AND_Gate
  and and_7 (addi_2, ~in_1[0], in_1[1], ~in_1[2], ~in_1[3], ~in_1[4], ~in_1[5]);  // AND_Gate
  and and_8 (ori, in_1[0], ~in_1[1], in_1[2], in_1[3], ~in_1[4], ~in_1[5]);  // AND_Gate
  and and_9 (bne, in_1[0], ~in_1[1], in_1[2], ~in_1[3], ~in_1[4], ~in_1[5]);  // AND_Gate
  and and_10 (sw, in_1[0], in_1[1], ~in_1[2], in_1[3], ~in_1[4], in_1[5]);  // AND_Gate
  and and_11 (xori, ~in_1[0], in_1[1], in_1[2], in_1[3], ~in_1[4], ~in_1[5]);  // AND_Gate
  and and_12 (blez, ~in_1[0], in_1[1], in_1[2], ~in_1[3], ~in_1[4], ~in_1[5]);  // AND_Gate
  and and_13 (slti, ~in_1[0], in_1[1], ~in_1[2], in_1[3], ~in_1[4], ~in_1[5]);  // AND_Gate
  and and_14 (bgtz, in_1[0], in_1[1], in_1[2], ~in_1[3], ~in_1[4], ~in_1[5]);  // AND_Gate

  // Other names for the same wires on the sheet: OpCode[5:0] = in_1

  // Notes on the sheet:
  //   Type I
  //   Type J
endmodule
