// Logisim project s-mips.circ as structural Verilog
module S_MIPS_Board (
  input  DESHABILITAR_DISPATCHER,
  output halt
);

  wire button_1_out, CLK, CS, d_ff_1_q, LCLR, LoadRAM, LoadRAMOn, LW, R_R_W, R_W, ram_dispatcher_1_finished,
       RCS, Reset_out, RST, TTY_EN;
  wire [2:0] KDB;
  wire [3:0] LMask, Mask, ram_1_read_time, ram_1_write_time, RMask;
  wire [6:0] KDB_DATA, TTY_DATA;
  wire [15:0] Addr, LAddr, RAddr;
  wire [31:0] I0, I1, I2, I3, LData, ram_1_data_out_0, ram_1_data_out_1, ram_1_data_out_2, ram_1_data_out_3,
       RI0, RI1, RI2, RI3;

  TTY #(.rows(25), .cols(80)) tty_1 (.data(TTY_DATA), .clk(CLK), .we(TTY_EN), .clr(RST));
  not not_1 (LoadRAMOn, ram_dispatcher_1_finished);
  RAM_Dispatcher ram_dispatcher_1 (
    .WriteTime(ram_1_write_time), .Clock(CLK), .Data(LData), .Address(LAddr), .Mask(LMask),
    .Finished(ram_dispatcher_1_finished), .Write(LW), .CLR(LCLR));
  Keyboard #(.buflen(64)) keyboard_1 (.clk(CLK), .re(KDB[0]), .avail(KDB[2]), .data(KDB_DATA));  // open: clr
  RAM ram_1 (
    .Address(RAddr), .Data_Out_0(ram_1_data_out_0), .Data_Out_1(ram_1_data_out_1),
    .Data_Out_2(ram_1_data_out_2), .Data_Out_3(ram_1_data_out_3), .Data_In_0(RI0), .Data_In_1(RI1),
    .Data_In_2(RI2), .Data_In_3(RI3), .Mask(RMask), .nRead_Write(R_R_W), .Chip_Select(RCS),
    .Read_Time(ram_1_read_time), .Reset(button_1_out), .Write_Time(ram_1_write_time));
  Button button_1 (.out(button_1_out));
  D_Flip_Flop d_ff_1 (.clk(CLK), .D(1'b1), .Q(d_ff_1_q), .reset(Reset_out));  // open: Qn, preset, en
  Button Reset (.out(Reset_out));
  S_MIPS s_mips_1 (
    .Kbd_Enable(KDB[0]), .Address(Addr), .Kbd_Clear(KDB[1]), .Kbd_Available(KDB[2]), .RAM_In_0(I0),
    .Kbd_ASCII_Data(KDB_DATA), .RAM_In_1(I1), .TTY_Enable(TTY_EN), .RAM_In_2(I2), .RAM_In_3(I3),
    .TTY_ASCII_Data(TTY_DATA), .Reset(RST), .Clock(CLK), .RAM_Out_1(ram_1_data_out_1), .Stop(halt),
    .RAM_Out_2(ram_1_data_out_2), .RAM_Out_3(ram_1_data_out_3), .Mask(Mask), .Read_Time(ram_1_read_time),
    .Write_Time(ram_1_write_time), .nRead_Write(R_W), .Chip_Select(CS), .RAM_Out_0(ram_1_data_out_0));
  D_Flip_Flop d_ff_2 (.clk(CLK), .D(d_ff_1_q), .Qn(LCLR), .reset(Reset_out));  // open: Q, preset, en
  or or_1 (RST, LCLR, LoadRAM);
  Clock clock_1 (.out(CLK));
  Multiplexer #(.width(32), .enable("false")) multiplexer_1 (.in0(I0), .in1(LData), .out(RI0), .sel(LoadRAM));
  Multiplexer #(.width(32), .enable("false")) multiplexer_2 (.in0(I1), .in1(LData), .out(RI1), .sel(LoadRAM));
  Multiplexer #(.width(32), .enable("false")) multiplexer_3 (.in0(I2), .in1(LData), .out(RI2), .sel(LoadRAM));
  Multiplexer #(.width(32), .enable("false")) multiplexer_4 (.in0(I3), .in1(LData), .out(RI3), .sel(LoadRAM));
  and and_1 (LoadRAM, ~DESHABILITAR_DISPATCHER, LoadRAMOn);  // AND_Gate
  Multiplexer #(.width(16), .enable("false")) multiplexer_5 (.in0(Addr), .in1(LAddr), .out(RAddr), .sel(LoadRAM));
  Multiplexer #(.width(4), .enable("false")) multiplexer_6 (.in0(Mask), .in1(LMask), .out(RMask), .sel(LoadRAM));
  Multiplexer #(.enable("false")) multiplexer_7 (.in0(CS), .in1(LW), .out(RCS), .sel(LoadRAM));
  Multiplexer #(.enable("false")) multiplexer_8 (.in0(R_W), .in1(LW), .out(R_R_W), .sel(LoadRAM));

  // Notes on the sheet:
  //   NO MODIFICAR
  //   Keyboard
endmodule

module RAM (
  input  [15:0] Address,
  input  [31:0] Data_In_0,
  input  [31:0] Data_In_1,
  input  [31:0] Data_In_2,
  input  [31:0] Data_In_3,
  input  [3:0] Mask,
  input  nRead_Write,
  input  Chip_Select,
  input  Reset,
  output [31:0] Data_Out_0,
  output [31:0] Data_Out_1,
  output [31:0] Data_Out_2,
  output [31:0] Data_Out_3,
  output [3:0] Read_Time,
  output [3:0] Write_Time
);

  wire and_2_out, and_3_out, and_4_out, and_5_out, and_6_out, and_7_out, and_8_out, and_9_out, Changed, CLK,
       comparator_2_eq, comparator_3_eq, comparator_4_eq, comparator_5_eq, comparator_6_eq, Count,
       demultiplexer_3_out0, Idle, Idle_q, Load, Load0, Load1, nand_1_out, or_1_out, or_2_out, or_3_out,
       or_4_out, or_5_out, or_6_out, or_7_out, or_8_out, or_9_out, or_10_out, Proc_q, Update_Mem, Zero_Time;
  wire [3:0] counter_1_q, multiplexer_1_out, subtractor_1_out;
  wire [31:0] register_1_q, register_2_q, register_3_q, register_4_q, register_5_q;

  // Probe on 4'b0011
  // Probe on 4'b0010
  Multiplexer #(.width(4), .enable("false")) multiplexer_1 (
    .in0(4'b0011), .in1(4'b0010), .out(multiplexer_1_out), .sel(nRead_Write));
  or or_1 (or_1_out, Idle, Update_Mem);
  or or_2 (or_2_out, ~Chip_Select, Reset);  // OR_Gate
  Subtractor #(.width(4)) subtractor_1 (.a(multiplexer_1_out), .b(4'b0010), .out(subtractor_1_out));  // open: bin, bout
  Demultiplexer #(.enable("false")) demultiplexer_1 (.out0(Idle), .out1(Load0), .in(Idle_q), .sel(Changed));
  D_Flip_Flop u_Idle (.clk(CLK), .D(or_1_out), .Q(Idle_q), .preset(or_2_out));  // open: Qn, en, reset
  // Probe on counter_1_q
  Counter #(.width(4), .max('hf)) counter_1 (
    .load(Load), .D(subtractor_1_out), .count(Count), .Q(counter_1_q), .clk(CLK), .clr(or_3_out));  // open: carry
  or or_3 (or_3_out, ~Chip_Select, Reset);  // OR_Gate
  Comparator #(.width(4), .mode("unsigned")) comparator_1 (
    .a(4'b0000), .b(counter_1_q), .eq(Zero_Time));  // open: gt, lt
  or or_4 (or_4_out, Count, Load0, Load1);
  Register #(.width(32)) register_1 (.D(Data_In_0), .en(Chip_Select), .Q(register_1_q), .clk(CLK), .clr(or_5_out));
  or or_5 (or_5_out, ~Chip_Select, Reset);  // OR_Gate
  Register #(.width(32)) register_2 (.D(Data_In_1), .en(Chip_Select), .Q(register_2_q), .clk(CLK), .clr(or_6_out));
  or or_6 (or_6_out, ~Chip_Select, Reset);  // OR_Gate
  Register #(.width(32)) register_3 (.D(Data_In_2), .en(Chip_Select), .Q(register_3_q), .clk(CLK), .clr(or_7_out));
  or or_7 (or_7_out, ~Chip_Select, Reset);  // OR_Gate
  Register #(.width(32)) register_4 (.D(Data_In_3), .en(Chip_Select), .Q(register_4_q), .clk(CLK), .clr(or_8_out));
  or or_8 (or_8_out, ~Chip_Select, Reset);  // OR_Gate
  Register #(.width(32)) register_5 (
    .D({{11{1'b1}}, nRead_Write, Mask, Address}), .en(Chip_Select), .Q(register_5_q), .clk(CLK),
    .clr(or_9_out));
  or or_9 (or_9_out, ~Chip_Select, Reset);  // OR_Gate
  D_Flip_Flop Proc (.clk(CLK), .D(or_4_out), .Q(Proc_q), .reset(or_10_out));  // open: Qn, preset, en
  or or_10 (or_10_out, ~Chip_Select, Reset);  // OR_Gate
  Demultiplexer #(.enable("false")) demultiplexer_2 (
    .out0(Count), .out1(Update_Mem), .in(demultiplexer_3_out0), .sel(Zero_Time));
  Demultiplexer #(.enable("false")) demultiplexer_3 (
    .out0(demultiplexer_3_out0), .out1(Load1), .in(Proc_q), .sel(Changed));
  Clock clock_1 (.out(CLK));
  Comparator #(.width(32)) comparator_2 (.a(register_1_q), .b(Data_In_0), .eq(comparator_2_eq));  // open: gt, lt
  Comparator #(.width(32)) comparator_3 (.a(register_2_q), .b(Data_In_1), .eq(comparator_3_eq));  // open: gt, lt
  Comparator #(.width(32)) comparator_4 (.a(register_3_q), .b(Data_In_2), .eq(comparator_4_eq));  // open: gt, lt
  Comparator #(.width(32)) comparator_5 (.a(register_4_q), .b(Data_In_3), .eq(comparator_5_eq));  // open: gt, lt
  Comparator #(.width(32)) comparator_6 (
    .a(register_5_q), .b({{11{1'b1}}, nRead_Write, Mask, Address}), .eq(comparator_6_eq));  // open: gt, lt
  nand nand_1 (nand_1_out, comparator_6_eq, comparator_2_eq, comparator_3_eq, comparator_4_eq, comparator_5_eq);
  and and_1 (Changed, nand_1_out, Chip_Select);
  or or_11 (Load, Count, Load1, Load0);
  and and_2 (and_2_out, Mask[0], Update_Mem, nRead_Write);
  and and_3 (and_3_out, Mask[1], Update_Mem, nRead_Write);
  and and_4 (and_4_out, Mask[2], Update_Mem, nRead_Write);
  and and_5 (and_5_out, Mask[3], Update_Mem, nRead_Write);
  RAM_part #(.addrWidth(16), .dataWidth(32), .bus("separate")) ram_1 (
    .addr(Address), .din(Data_In_0), .data(Data_Out_0), .str(and_2_out), .sel(Chip_Select), .clk(CLK),
    .ld(and_6_out), .clr(Reset));
  and and_6 (and_6_out, ~nRead_Write, Idle);  // AND_Gate
  RAM_part #(.addrWidth(16), .dataWidth(32), .bus("separate")) ram_2 (
    .addr(Address), .din(Data_In_1), .data(Data_Out_1), .str(and_3_out), .sel(Chip_Select), .clk(CLK),
    .ld(and_7_out), .clr(Reset));
  and and_7 (and_7_out, ~nRead_Write, Idle);  // AND_Gate
  RAM_part #(.addrWidth(16), .dataWidth(32), .bus("separate")) ram_3 (
    .addr(Address), .din(Data_In_2), .data(Data_Out_2), .str(and_4_out), .sel(Chip_Select), .clk(CLK),
    .ld(and_8_out), .clr(Reset));
  and and_8 (and_8_out, ~nRead_Write, Idle);  // AND_Gate
  RAM_part #(.addrWidth(16), .dataWidth(32), .bus("separate")) ram_4 (
    .addr(Address), .din(Data_In_3), .data(Data_Out_3), .str(and_5_out), .sel(Chip_Select), .clk(CLK),
    .ld(and_9_out), .clr(Reset));
  and and_9 (and_9_out, ~nRead_Write, Idle);  // AND_Gate

  assign Read_Time = 4'b0011;
  assign Write_Time = 4'b0010;

  // Other names for the same wires on the sheet: M0 = Mask[0]; M1 = Mask[1]; M2 = Mask[2]; M3 = Mask[3];
  //   RW = nRead_Write; CLR = Reset; CS = Chip_Select; Load2 = Count

  // Notes on the sheet:
  //   NO MODIFICAR
  //   excepto quizás los valores RT y WT
  //   BANK0
  //   BANK1
  //   BANK2
  //   BANK3
endmodule

module S_MIPS (
  input  Kbd_Available,
  input  [6:0] Kbd_ASCII_Data,
  input  [31:0] RAM_Out_0,
  input  [31:0] RAM_Out_1,
  input  Reset,
  input  [31:0] RAM_Out_2,
  input  Clock,
  input  [31:0] RAM_Out_3,
  input  [3:0] Read_Time,
  input  [3:0] Write_Time,
  output Kbd_Enable,
  output [15:0] Address,
  output Kbd_Clear,
  output TTY_Enable,
  output [6:0] TTY_ASCII_Data,
  output Stop,
  output [31:0] RAM_In_0,
  output [31:0] RAM_In_1,
  output [31:0] RAM_In_2,
  output [31:0] RAM_In_3,
  output [3:0] Mask,
  output nRead_Write,
  output Chip_Select
);

  wire and_3_out, comparator_1_lt, comparator_2_eq, comparator_3_eq, d_ff_4_q, d_ff_5_q, d_ff_10_q,
       d_ff_11_q, Decoder_En, demultiplexer_1_out0, demultiplexer_1_out1, demultiplexer_3_out0,
       demultiplexer_5_out0, demultiplexer_6_out1, Final, INC, INC1, INC2, kbd, LoadWord, LoadWord1,
       LoadWord2, lw, lw1, or_2_out, or_3_out, or_4_out, or_6_out, or_7_out, or_8_out, or_9_out, or_10_out,
       or_11_out, or_12_out, or_13_out, or_15_out, or_17_out, or_18_out, or_19_out, PC_En, POP, POP1, pop1_t,
       POP2, pop_t, push, R_End, Reader_CS, Reader_En, Reading, stack, stack1, sw, tty, W_End, W_Final,
       Writter_CS, Writter_En;
  wire [3:0] adder_1_out, adder_2_out, adder_4_out, counter_1_q, counter_2_q, counter_3_q, Read_Mask,
       Write_Mask;
  wire [4:0] Rd, Rd_pop, Rt, Rt_lw;
  wire [15:0] Read_ADDR, Write_ADDR;
  wire [31:0] Constant_32b, Instruction, multiplexer_3_out, multiplexer_5_out, PC_Out, RAM_Input,
       ReaderAddress, register_3_q, SP, Value_1, Word_Address, WritterAddress;

  or or_1 (LoadWord, LoadWord1, LoadWord2);
  or or_2 (or_2_out, demultiplexer_1_out0, lw);
  Register #(.width(5)) register_1 (.D(Rt), .en(lw), .Q(Rt_lw), .clk(Clock), .clr(Reset));
  Demultiplexer #(.enable("false")) demultiplexer_1 (
    .out0(demultiplexer_1_out0), .out1(demultiplexer_1_out1), .in(LoadWord1), .sel(LoadWord1));
  D_Flip_Flop d_ff_1 (.clk(Clock), .D(or_2_out), .Q(LoadWord1), .reset(or_3_out));  // open: Qn, preset, en
  or or_3 (or_3_out, Reset, lw1);
  Counter #(.width(4), .max('h8)) counter_1 (
    .count(INC), .Q(counter_1_q), .clk(Clock), .clr(or_4_out));  // open: load, D, carry
  or or_4 (or_4_out, Reset, demultiplexer_1_out1);
  Multiplexer #(.width(4), .enable("false")) multiplexer_1 (
    .in0(Read_Mask), .in1(Write_Mask), .out(Mask), .sel(nRead_Write));
  or or_5 (Chip_Select, Reader_CS, Writter_CS);
  or or_6 (or_6_out, INC, demultiplexer_1_out1);
  Demultiplexer #(.enable("false")) demultiplexer_2 (.out0(INC), .out1(lw1), .in(LoadWord2), .sel(comparator_1_lt));
  D_Flip_Flop d_ff_2 (.clk(Clock), .D(or_6_out), .Q(LoadWord2), .reset(Reset));  // open: Qn, preset, en
  Comparator #(.width(4)) comparator_1 (.a(counter_1_q), .b(adder_1_out), .lt(comparator_1_lt));  // open: gt, eq
  Adder #(.width(4)) adder_1 (.a(Read_Time), .b(4'b0001), .out(adder_1_out));  // open: cin, cout
  and and_1 (TTY_Enable, tty, Final);
  and and_2 (Kbd_Enable, kbd, Decoder_En);
  MemoryReader memoryreader_1 (
    .in_1(RAM_Out_0), .in_2(RAM_Out_1), .in_3(RAM_Out_2), .in_4(RAM_Out_3), .in_5(ReaderAddress),
    .in_6(Reader_En), .in_7(Reset), .in_8(Clock), .in_9(Read_Time), .CS(Reader_CS), .Reading(Reading),
    .Instruction(Instruction), .Address(Read_ADDR), .Final(R_End), .out_11(Read_Mask));
  or or_7 (or_7_out, sw, push);
  and and_3 (and_3_out, ~or_7_out, Final);  // AND_Gate
  or or_8 (or_8_out, demultiplexer_3_out0, pop_t);
  or or_9 (or_9_out, Reset, pop1_t);
  Register #(.width(5)) register_2 (.D(Rd), .en(pop_t), .Q(Rd_pop), .clk(Clock), .clr(Reset));
  Multiplexer #(.width(16), .enable("false")) multiplexer_2 (
    .in0(Read_ADDR), .in1(Write_ADDR), .out(Address), .sel(nRead_Write));
  D_Flip_Flop d_ff_3 (.clk(Clock), .D(and_3_out), .Q(Reader_En), .preset(Reset), .reset(Stop));  // open: Qn, en
  or or_10 (or_10_out, Reset, Final);
  D_Flip_Flop d_ff_4 (.clk(Clock), .D(or_8_out), .Q(d_ff_4_q), .reset(or_9_out));  // open: Qn, preset, en
  Demultiplexer #(.enable("false")) demultiplexer_3 (
    .out0(demultiplexer_3_out0), .out1(POP1), .in(d_ff_4_q), .sel(d_ff_4_q));
  Counter #(.width(4), .max('h8)) counter_2 (
    .count(INC2), .Q(counter_2_q), .clk(Clock), .clr(or_11_out));  // open: load, D, carry
  or or_11 (or_11_out, Reset, POP1);
  Multiplexer #(.width(32), .enable("false")) multiplexer_3 (
    .in0(PC_Out), .in1(Word_Address), .out(multiplexer_3_out), .sel(d_ff_5_q));
  D_Flip_Flop d_ff_5 (.clk(Clock), .Q(d_ff_5_q), .preset(lw), .reset(or_10_out));  // open: D, Qn, en
  Multiplexer #(.width(32), .enable("false")) multiplexer_4 (
    .in0(multiplexer_3_out), .in1(SP), .out(ReaderAddress), .sel(POP));
  D_Flip_Flop d_ff_6 (.clk(Clock), .D(or_12_out), .Q(POP2), .reset(Reset));  // open: Qn, preset, en
  or or_12 (or_12_out, INC2, POP1);
  Adder #(.width(4)) adder_2 (.a(Read_Time), .b(4'b0001), .out(adder_2_out));  // open: cin, cout
  DataPath datapath_1 (
    .in_3(Instruction), .in_4(Clock), .in_5(Reset), .in_6(Final), .in_7(Decoder_En), .in_9(Kbd_Available),
    .in_10(Kbd_ASCII_Data), .out_15(Constant_32b), .out_16(TTY_ASCII_Data), .out_18(PC_Out), .out_22(SP),
    .out_17(pop_t), .out_20(push), .out_24(lw), .out_27(sw), .out_23(Stop), .out_13(RAM_Input), .out_26(tty),
    .in_8(PC_En), .out_25(kbd), .out_14(Value_1), .in_11(pop1_t), .in_1(Rd_pop), .out_21(Rd), .out_19(Rt),
    .RtLo(Rt_lw), .in_12(lw1));
  MemoryWritter memorywritter_1 (
    .in_1(RAM_Input), .in_2(WritterAddress), .in_3(Clock), .in_4(Reset), .in_5(Writter_En),
    .in_6(Write_Time), .Ram_0(RAM_In_0), .Writting(nRead_Write), .Mask(Write_Mask), .Ram_1(RAM_In_1),
    .Address_Out(Write_ADDR), .CS(Writter_CS), .Ram_2(RAM_In_2), .Ram_3(RAM_In_3), .Final(W_End));
  D_Flip_Flop d_ff_7 (.clk(Clock), .D(or_13_out), .Q(Writter_En), .reset(Reset));  // open: Qn, preset, en
  or or_13 (or_13_out, push, sw);
  Demultiplexer #(.enable("false")) demultiplexer_4 (.out0(INC2), .out1(pop1_t), .in(POP2), .sel(comparator_2_eq));
  Comparator #(.width(4)) comparator_2 (.a(counter_2_q), .b(adder_2_out), .eq(comparator_2_eq));  // open: gt, lt
  or or_14 (Final, W_Final, Decoder_En);
  or or_15 (or_15_out, demultiplexer_5_out0, push);
  or or_16 (stack, stack1, INC1);
  D_Flip_Flop d_ff_8 (.clk(Clock), .D(R_End), .Q(Decoder_En), .reset(Reset));  // open: Qn, preset, en
  D_Flip_Flop d_ff_9 (.clk(Clock), .D(W_End), .Q(W_Final), .reset(Reset));  // open: Qn, preset, en
  Register #(.width(32)) register_3 (.D(Value_1), .en(1'b1), .Q(register_3_q), .clk(Clock), .clr(Reset));
  D_Flip_Flop d_ff_10 (.clk(Clock), .D(or_15_out), .Q(d_ff_10_q), .reset(or_17_out));  // open: Qn, preset, en
  Demultiplexer #(.enable("false")) demultiplexer_5 (
    .out0(demultiplexer_5_out0), .out1(stack1), .in(d_ff_10_q), .sel(d_ff_10_q));
  or or_17 (or_17_out, Reset, demultiplexer_6_out1);
  and and_4 (PC_En, Decoder_En, ~POP, ~LoadWord);  // AND_Gate
  Multiplexer #(.width(32), .enable("false")) multiplexer_5 (
    .in0(Word_Address), .in1(SP), .out(multiplexer_5_out), .sel(stack));
  Counter #(.width(4), .max('h8)) counter_3 (
    .count(INC1), .Q(counter_3_q), .clk(Clock), .clr(or_18_out));  // open: load, D, carry
  or or_18 (or_18_out, Reset, stack1);
  Multiplexer #(.width(32), .enable("false")) multiplexer_6 (
    .in0(multiplexer_5_out), .in1({32{1'b0}}), .out(WritterAddress), .sel(Reset));
  Adder #(.width(32)) adder_3 (.a(register_3_q), .b(Constant_32b), .out(Word_Address));  // open: cin, cout
  D_Flip_Flop d_ff_11 (.clk(Clock), .D(or_19_out), .Q(d_ff_11_q));  // open: Qn, preset, en, reset
  or or_19 (or_19_out, INC1, stack1);
  Demultiplexer #(.enable("false")) demultiplexer_6 (
    .out0(INC1), .out1(demultiplexer_6_out1), .in(d_ff_11_q), .sel(comparator_3_eq));
  Comparator #(.width(4)) comparator_3 (.a(counter_3_q), .b(adder_4_out), .eq(comparator_3_eq));  // open: gt, lt
  Adder #(.width(4)) adder_4 (.a(Write_Time), .b(4'b0001), .out(adder_4_out));  // open: cin, cout
  // NOT_Gate not_1 is placed but not wired
  or or_20 (POP, POP1, pop1_t, POP2);

  assign Kbd_Clear = Reset;

  // Other names for the same wires on the sheet: CLK = Clock; CS = Chip_Select; halt = Stop;
  //   KBD_AVAIL = Kbd_Available; CLR = Reset; KBD_CLR = Reset; KBD_DATA[6:0] = Kbd_ASCII_Data; R_Final = Decoder_En;
  //   RAM_A[15:0] = Address; RAM_INPUT_0[31:0] = RAM_In_0; RAM_INPUT_1[31:0] = RAM_In_1; RAM_INPUT_2[31:0] = RAM_In_2;
  //   RAM_INPUT_3[31:0] = RAM_In_3; RAM_MASK[3:0] = Mask; RamOut_0[31:0] = RAM_Out_0; RamOut_1[31:0] = RAM_Out_1;
  //   RamOut_2[31:0] = RAM_Out_2; RamOut_3[31:0] = RAM_Out_3; SAd[1:0] = {pop_t, lw}; stack2 = INC1;
  //   TTY_DATA[6:0] = TTY_ASCII_Data; RW = nRead_Write; Writting = nRead_Write

  // Notes on the sheet:
  //   RAM ADDRESS
  //   DATA FROM RAM
  //   DATA TO RAM
  //   DATA WRITE MASK
  //   RAM TIMING
  //   RAM CONTROL
  //   KEYBOARD
  //   TTY
  //   SEQUENCING
endmodule

module RAM_Dispatcher (
  input  [3:0] WriteTime,
  input  Clock,
  input  CLR,
  output [31:0] Data,
  output [15:0] Address,
  output [3:0] Mask,
  output Finished,
  output Write
);

  wire demultiplexer_2_out1, demultiplexer_3_out1, End, IDLE_q, IncAddr, Load, or_1_out, or_2_out, While_q,
       WriteEnd;
  wire [3:0] counter_1_q;
  wire [31:0] CurrentAddress_q;

  Counter #(.width(32), .max('hffffffff)) CurrentAddress (
    .count(IncAddr), .Q({CurrentAddress_q[31:18], Address, CurrentAddress_q[1:0]}), .clk(Clock), .clr(CLR));  // open: load, D, carry
  or or_1 (or_1_out, IncAddr, demultiplexer_3_out1, Finished);
  D_Flip_Flop IDLE (.clk(Clock), .D(or_1_out), .Q(IDLE_q), .preset(CLR));  // open: Qn, en, reset
  Demultiplexer #(.enable("false")) demultiplexer_1 (.out0(Load), .out1(Finished), .in(IDLE_q), .sel(End));
  D_Flip_Flop While (.clk(Clock), .D(or_2_out), .Q(While_q), .reset(CLR));  // open: Qn, preset, en
  or or_2 (or_2_out, Write, Load);
  RAM_part #(.addrWidth(18), .dataWidth(32)) ram_1 (
    .addr({Address, CurrentAddress_q[1:0]}), .data(Data), .clk(Clock));  // open: sel, ld, clr
  Demultiplexer #(.enable("false")) demultiplexer_2 (
    .out0(Write), .out1(demultiplexer_2_out1), .in(While_q), .sel(WriteEnd));
  Decoder #(.select(2)) decoder_1 (
    .out0(Mask[0]), .out1(Mask[1]), .out2(Mask[2]), .out3(Mask[3]), .sel(CurrentAddress_q[1:0]));  // open: en
  Demultiplexer #(.enable("false")) demultiplexer_3 (
    .out0(IncAddr), .out1(demultiplexer_3_out1), .in(demultiplexer_2_out1), .sel(End));
  Counter #(.width(4), .max('hf)) counter_1 (
    .load(Load), .D(WriteTime), .count(Write), .Q(counter_1_q), .clk(Clock));  // open: carry, clr
  Comparator #(.width(32)) comparator_1 (.a(Data), .b({32{1'b1}}), .eq(End));  // open: gt, lt
  Comparator #(.width(4)) comparator_2 (.a(4'b0000), .b(counter_1_q), .eq(WriteEnd));  // open: gt, lt

  // Other names for the same wires on the sheet: CLK = Clock; Count = Write; WT[3:0] = WriteTime
endmodule

module ALU (
  input  [31:0] A,
  input  [31:0] B,
  input  in_3,
  input  in_4,
  input  [5:0] FuncCode,
  output NF,
  output [31:0] Result,
  output ZF,
  output [31:0] Hi,
  output [31:0] Lo
);

  wire A___B_signed_t, A___B_t_t_t_t, A___B_unsigned_t, comparator_5_lt, comparator_6_lt, div, divu,
       Hi_Enable, mult, mult_multu, multu, multu_divu, N, not_1_out;
  wire [3:0] Sel_Op;
  wire [31:0] A____B, A___B, A___B_Hi, A___B_Lo, A___B_signed, A___B_t, A___B_t_t, A___B_t_t_t,
       A___B_t_t_t_t_t, A___B_unsigned, A_xor_B, multiplexer_2_out, multiplexer_3_out, not_2_out, Resto;

  Op_Decoder op_decoder_1 (.in_1(FuncCode), .Output(Sel_Op));
  Comparator #(.width(6), .mode("unsigned")) comparator_1 (.a(FuncCode), .b(6'b011000), .eq(mult));  // open: gt, lt
  Comparator #(.width(6), .mode("unsigned")) comparator_2 (.a(FuncCode), .b(6'b011001), .eq(multu));  // open: gt, lt
  Comparator #(.width(6), .mode("unsigned")) comparator_3 (.a(FuncCode), .b(6'b011011), .eq(divu));  // open: gt, lt
  Comparator #(.width(6), .mode("unsigned")) comparator_4 (.a(FuncCode), .b(6'b011010), .eq(div));  // open: gt, lt
  Adder #(.width(32)) adder_1 (.a(A), .b(B), .out(A___B_t));  // open: cin, cout
  Subtractor #(.width(32)) subtractor_1 (.a(A), .b(B), .out(A___B_t_t));  // open: bin, bout
  assign A___B = A & B;  // AND_Gate and_1, 32 bits wide
  assign A_xor_B = A ^ B;  // XOR_Gate xor_1, 32 bits wide
  or or_1 (mult_multu, mult, multu);
  or or_2 (multu_divu, multu, divu);
  assign A___B_t_t_t_t_t = A | B;  // OR_Gate or_3, 32 bits wide
  assign A____B = ~(A | B);  // NOR_Gate nor_1, 32 bits wide
  Multiplicacion multiplicacion_1 (.in_1(A), .in_2(B), .in_3(mult), .Lo(A___B_Lo), .Hi(A___B_Hi));
  Division division_1 (.in_1(A), .in_2(B), .Signed(div), .Output(A___B_t_t_t), .Resto(Resto));
  Comparator #(.width(32)) comparator_5 (.a(A), .b(B), .gt(A___B_signed_t), .eq(A___B_t_t_t_t), .lt(comparator_5_lt));
  Comparator #(.width(32), .mode("unsigned")) comparator_6 (
    .a(A), .b(B), .gt(A___B_unsigned_t), .lt(comparator_6_lt));  // open: eq
  or or_4 (Hi_Enable, mult_multu, multu_divu, div);
  assign A___B_signed = {{31{1'b0}}, comparator_5_lt};  // Bit_Extender bit_extender_1
  assign A___B_unsigned = {{31{1'b0}}, comparator_6_lt};  // Bit_Extender bit_extender_2
  not not_1 (not_1_out, multu_divu);
  and and_2 (NF, N, not_1_out);
  assign not_2_out = ~A___B_t_t_t_t_t;  // NOT_Gate not_2, 32 bits wide
  Multiplexer #(.select(4), .width(32), .enable("false")) multiplexer_1 (
    .in0(A___B_t), .in1(A___B_signed), .in2(A___B_unsigned), .in3(A___B), .in4(A___B_t_t_t_t_t),
    .in5(A_xor_B), .in6(A___B_Hi), .in7(A___B_t_t_t), .in8(A___B_t_t), .in9(not_2_out), .out(Result),
    .sel(Sel_Op));  // open: in10, in11, in12, in13, in14, in15
  // Probe on Result
  Multiplexer #(.width(32), .enable("false")) multiplexer_2 (
    .in0(A___B_Hi), .in1(Resto), .out(multiplexer_2_out), .sel(FuncCode[1]));
  Multiplexer #(.width(32), .enable("false")) multiplexer_3 (
    .in0(A___B_Lo), .in1(A___B_t_t_t), .out(multiplexer_3_out), .sel(FuncCode[1]));
  Comparator #(.width(32)) comparator_7 (.a(Result), .b({32{1'b0}}), .eq(ZF), .lt(N));  // open: gt
  Register #(.width(32)) u_Lo (.D(multiplexer_2_out), .en(Hi_Enable), .Q(Hi), .clk(in_3), .clr(in_4));
  Register #(.width(32)) u_Hi (.D(multiplexer_3_out), .en(Hi_Enable), .Q(Lo), .clk(in_3), .clr(in_4));

  // Other names for the same wires on the sheet: CLK = in_3; Lo_Enable = Hi_Enable; RST = in_4
endmodule

module Multiplicacion (
  input  [31:0] in_1,
  input  [31:0] in_2,
  input  in_3,
  output [31:0] Lo,
  output [31:0] Hi
);

  wire adder_1_cout, adder_3_cout, adder_5_cout, and_1_out;
  wire [31:0] adder_1_out, adder_2_out, adder_3_out, adder_4_out, Hi_S, Hi_U, Lo_S, Lo_U, multiplexer_5_out,
       multiplexer_6_out, X, Y;

  Multiplier #(.width(32)) multiplier_1 (.a(X), .b(Y), .out(Lo_S), .cout(Hi_S));  // open: cin
  Multiplexer #(.width(32), .enable("false")) multiplexer_1 (.in0({1'b0, in_1[31:1]}), .in1(in_1), .out(X), .sel(in_3));
  Multiplexer #(.width(32), .enable("false")) multiplexer_2 (.in0({1'b0, in_2[31:1]}), .in1(in_2), .out(Y), .sel(in_3));
  Multiplexer #(.width(32), .enable("false")) multiplexer_3 (.in0(Lo_U), .in1(Lo_S), .out(Lo), .sel(in_3));
  Multiplexer #(.width(32), .enable("false")) multiplexer_4 (.in0(Hi_U), .in1(Hi_S), .out(Hi), .sel(in_3));
  Multiplexer #(.width(32), .enable("false")) multiplexer_5 (
    .in0({32{1'b0}}), .in1({in_2[31:1], 1'b0}), .out(multiplexer_5_out), .sel(in_1[0]));
  Adder #(.width(32)) adder_1 (
    .a({Lo_S[29:0], 2'b00}), .b(multiplexer_5_out), .out(adder_1_out), .cout(adder_1_cout));  // open: cin
  Adder #(.width(32)) adder_2 (
    .a({32{1'b0}}), .b({Hi_S[29:0], Lo_S[31:30]}), .out(adder_2_out), .cin(adder_1_cout));  // open: cout
  Adder #(.width(32)) adder_3 (
    .a(adder_1_out), .b(multiplexer_6_out), .out(adder_3_out), .cout(adder_3_cout));  // open: cin
  Multiplexer #(.width(32), .enable("false")) multiplexer_6 (
    .in0({32{1'b0}}), .in1({in_1[31:1], 1'b0}), .out(multiplexer_6_out), .sel(in_2[0]));
  Adder #(.width(32)) adder_4 (.a(adder_2_out), .b({32{1'b0}}), .out(adder_4_out), .cin(adder_3_cout));  // open: cout
  and and_1 (and_1_out, in_2[0], in_1[0]);
  Adder #(.width(32)) adder_5 (.a({32{1'b0}}), .b(adder_3_out), .out(Lo_U), .cin(and_1_out), .cout(adder_5_cout));
  Adder #(.width(32)) adder_6 (.a(adder_4_out), .b({32{1'b0}}), .out(Hi_U), .cin(adder_5_cout));  // open: cout

  // Other names for the same wires on the sheet: A[31:0] = in_1; A0 = in_1[0]; B[31:0] = in_2; B0 = in_2[0];
  //   shl_A[30:0] = in_1[31:1]; shr_A[31:1] = in_1[31:1]; shl_B[30:0] = in_2[31:1]; shr_B[31:1] = in_2[31:1];
  //   Signed = in_3
endmodule

module Division (
  input  [31:0] in_1,
  input  [31:0] in_2,
  input  Signed,
  output [31:0] Output,
  output [31:0] Resto
);

  wire Sign_Den, Sign_Num, Sign_Result;
  wire [31:0] Den, minus_A, minus_B, negator_1_out, negator_2_out, Num, Resto_t, Result;

  and and_1 (Sign_Num, Signed, in_2[31]);
  Multiplexer #(.width(32), .enable("false")) multiplexer_1 (.in0(in_1), .in1(minus_A), .out(Num), .sel(Sign_Num));
  and and_2 (Sign_Den, Signed, in_1[31]);
  xor xor_1 (Sign_Result, Sign_Den, Sign_Num);
  Multiplexer #(.width(32), .enable("false")) multiplexer_2 (.in0(in_2), .in1(minus_B), .out(Den), .sel(Sign_Den));
  Negator #(.width(32)) negator_1 (.in(Resto_t), .out(negator_1_out));
  Negator #(.width(32)) negator_2 (.in(Result), .out(negator_2_out));
  Negator #(.width(32)) negator_3 (.in(in_1), .out(minus_A));
  Negator #(.width(32)) negator_4 (.in(in_2), .out(minus_B));
  Divider #(.width(32)) divider_1 (.a(Num), .b(Den), .out(Result), .rem(Resto_t));  // open: upper
  Multiplexer #(.width(32), .enable("false")) multiplexer_3 (
    .in0(Resto_t), .in1(negator_1_out), .out(Resto), .sel(Sign_Result));
  Multiplexer #(.width(32), .enable("false")) multiplexer_4 (
    .in0(Result), .in1(negator_2_out), .out(Output), .sel(Sign_Result));

  // Other names for the same wires on the sheet: A[31:0] = in_1; A_Neg = in_1[31]; B[31:0] = in_2; B_Neg = in_2[31];
  //   Out_Resto[31:0] = Resto; Out_Result[31:0] = Output
endmodule

module RegisterFile (
  input  [31:0] Input,
  input  RST,
  input  in_3,
  input  in_4,
  input  [4:0] in_5,
  input  [4:0] in_6,
  input  [4:0] in_7,
  input  in_8,
  input  in_9,
  output [31:0] SP_Output,
  output [31:0] A,
  output [31:0] B
);

  wire en_R00, en_R01, en_R02, en_R03, en_R04, en_R05, en_R06, en_R07, en_R08, en_R09, en_R10, en_R11,
       en_R12, en_R13, en_R14, en_R15, en_R16, en_R17, en_R18, en_R19, en_R20, en_R21, en_R22, en_R23,
       en_R24, en_R25, en_R26, en_R27, en_R28, en_R29, en_R30, en_R31, using_stack;
  wire [31:0] multiplexer_3_out, R01_out, R02_out, R03_out, R04_out, R05_out, R06_out, R07_out, R08_out,
       R09_out, R10_out, R11_out, R12_out, R13_out, R14_out, R15_out, R16_out, R17_out, R18_out, R19_out,
       R20_out, R21_out, R22_out, R23_out, R24_out, R25_out, R26_out, R27_out, R28_out, R29_out, R30_out,
       SP_4, SP_4_t, undriven;

  Register #(.width(32)) R01 (.D(Input), .en(en_R01), .Q(R01_out), .clk(in_3), .clr(RST));
  Register #(.width(32)) R09 (.D(Input), .en(en_R09), .Q(R09_out), .clk(in_3), .clr(RST));
  Register #(.width(32)) R17 (.D(Input), .en(en_R17), .Q(R17_out), .clk(in_3), .clr(RST));
  Register #(.width(32)) R25 (.D(Input), .en(en_R25), .Q(R25_out), .clk(in_3), .clr(RST));
  Register #(.width(32)) R02 (.D(Input), .en(en_R02), .Q(R02_out), .clk(in_3), .clr(RST));
  Register #(.width(32)) R10 (.D(Input), .en(en_R10), .Q(R10_out), .clk(in_3), .clr(RST));
  Register #(.width(32)) R18 (.D(Input), .en(en_R18), .Q(R18_out), .clk(in_3), .clr(RST));
  Register #(.width(32)) R26 (.D(Input), .en(en_R26), .Q(R26_out), .clk(in_3), .clr(RST));
  Multiplexer #(.select(5), .width(32), .enable("false")) multiplexer_1 (
    .in0({32{1'b0}}), .in1(R01_out), .in2(R02_out), .in3(R03_out), .in4(R04_out), .in5(R05_out),
    .in6(R06_out), .in7(R07_out), .in8(R08_out), .in9(R09_out), .in10(R10_out), .in11(R11_out),
    .in12(R12_out), .in13(R13_out), .in14(R14_out), .in15(R15_out), .in16(R16_out), .in17(R17_out),
    .in18(R18_out), .in19(R19_out), .in20(R20_out), .in21(R21_out), .in22(R22_out), .in23(R23_out),
    .in24(R24_out), .in25(R25_out), .in26(R26_out), .in27(R27_out), .in28(R28_out), .in29(R29_out),
    .in30(R30_out), .in31(SP_Output), .out(A), .sel(in_5));
  Register #(.width(32)) R03 (.D(Input), .en(en_R03), .Q(R03_out), .clk(in_3), .clr(RST));
  Register #(.width(32)) R11 (.D(Input), .en(en_R11), .Q(R11_out), .clk(in_3), .clr(RST));
  Register #(.width(32)) R19 (.D(Input), .en(en_R19), .Q(R19_out), .clk(in_3), .clr(RST));
  Register #(.width(32)) R27 (.D(Input), .en(en_R27), .Q(R27_out), .clk(in_3), .clr(RST));
  Register #(.width(32)) R04 (.D(Input), .en(en_R04), .Q(R04_out), .clk(in_3), .clr(RST));
  Register #(.width(32)) R12 (.D(Input), .en(en_R12), .Q(R12_out), .clk(in_3), .clr(RST));
  Register #(.width(32)) R20 (.D(Input), .en(en_R20), .Q(R20_out), .clk(in_3), .clr(RST));
  Register #(.width(32)) R28 (.D(Input), .en(en_R28), .Q(R28_out), .clk(in_3), .clr(RST));
  Multiplexer #(.select(5), .width(32), .enable("false")) multiplexer_2 (
    .in0({32{1'b0}}), .in1(R01_out), .in2(R02_out), .in3(R03_out), .in4(R04_out), .in5(R05_out),
    .in6(R06_out), .in7(R07_out), .in8(R08_out), .in9(R09_out), .in10(R10_out), .in11(R11_out),
    .in12(R12_out), .in13(R13_out), .in14(R14_out), .in15(R15_out), .in16(undriven), .in17(R17_out),
    .in18(R18_out), .in19(R19_out), .in20(R20_out), .in21(R21_out), .in22(R22_out), .in23(R23_out),
    .in24(R24_out), .in25(R25_out), .in26(R26_out), .in27(R27_out), .in28(R28_out), .in29(R29_out),
    .in30(R30_out), .in31(SP_Output), .out(B), .sel(in_6));
  Register #(.width(32)) R05 (.D(Input), .en(en_R05), .Q(R05_out), .clk(in_3), .clr(RST));
  Register #(.width(32)) R13 (.D(Input), .en(en_R13), .Q(R13_out), .clk(in_3), .clr(RST));
  Register #(.width(32)) R21 (.D(Input), .en(en_R21), .Q(R21_out), .clk(in_3), .clr(RST));
  Register #(.width(32)) R29 (.D(Input), .en(en_R29), .Q(R29_out), .clk(in_3), .clr(RST));
  Demultiplexer #(.select(5), .enable("false")) demultiplexer_1 (
    .out0(en_R00), .out1(en_R01), .out2(en_R02), .out3(en_R03), .out4(en_R04), .out5(en_R05), .out6(en_R06),
    .out7(en_R07), .out8(en_R08), .out9(en_R09), .out10(en_R10), .out11(en_R11), .out12(en_R12),
    .out13(en_R13), .out14(en_R14), .out15(en_R15), .out16(en_R16), .out17(en_R17), .out18(en_R18),
    .out19(en_R19), .out20(en_R20), .out21(en_R21), .out22(en_R22), .out23(en_R23), .out24(en_R24),
    .out25(en_R25), .out26(en_R26), .out27(en_R27), .out28(en_R28), .out29(en_R29), .out30(en_R30),
    .out31(en_R31), .in(in_4), .sel(in_7));
  Register #(.width(32)) R06 (.D(Input), .en(en_R06), .Q(R06_out), .clk(in_3), .clr(RST));
  Register #(.width(32)) R14 (.D(Input), .en(en_R14), .Q(R14_out), .clk(in_3), .clr(RST));
  Register #(.width(32)) R22 (.D(Input), .en(en_R22), .Q(R22_out), .clk(in_3), .clr(RST));
  Register #(.width(32)) R30 (.D(Input), .en(en_R30), .Q(R30_out), .clk(in_3), .clr(RST));
  Register #(.width(32)) R07 (.D(Input), .en(en_R07), .Q(R07_out), .clk(in_3), .clr(RST));
  Register #(.width(32)) R15 (.D(Input), .en(en_R15), .Q(R15_out), .clk(in_3), .clr(RST));
  Register #(.width(32)) R23 (.D(Input), .en(en_R23), .Q(R23_out), .clk(in_3), .clr(RST));
  Multiplexer #(.width(32), .enable("false")) multiplexer_3 (
    .in0(SP_4_t), .in1(SP_4), .out(multiplexer_3_out), .sel(in_9));
  Register #(.width(32)) R08 (.D(Input), .en(en_R08), .Q(R08_out), .clk(in_3), .clr(RST));
  Register #(.width(32)) R16 (.D(Input), .en(en_R16), .Q(R16_out), .clk(in_3), .clr(RST));
  Register #(.width(32)) R24 (.D(Input), .en(en_R24), .Q(R24_out), .clk(in_3), .clr(RST));
  Subtractor #(.width(32)) subtractor_1 (.a(SP_Output), .b(32'h4), .out(SP_4_t));  // open: bin, bout
  Adder #(.width(32)) adder_1 (.a(SP_Output), .b(32'h4), .out(SP_4));  // open: cin, cout
  or or_1 (using_stack, in_8, in_9);
  Register #(.width(32)) R31 (.D(multiplexer_3_out), .en(using_stack), .Q(SP_Output), .clk(in_3), .clr(RST));
  // NOT_Gate not_1 is placed but not wired

  // Other names for the same wires on the sheet: CLK = in_3; Enable = in_4; Pop = in_9; Push = in_8;
  //   Read_1[4:0] = in_5; Read_2[4:0] = in_6; SP[31:0] = SP_Output; Write_Sel[4:0] = in_7
endmodule

module PC (
  input  [31:0] in_1,
  input  in_2,
  input  in_3,
  input  in_4,
  output [31:0] Output
);

  Register #(.width(32)) register_1 (.D(in_1), .en(in_2), .Q(Output), .clk(in_3), .clr(in_4));

  // Other names for the same wires on the sheet: CLK = in_3; Enable = in_2; PC_Input[31:0] = in_1; RST = in_4
endmodule

module BranchControlUnit (
  input  [31:0] in_1,
  input  [25:0] in_2,
  input  in_3,
  input  in_4,
  input  in_5,
  input  in_6,
  input  in_7,
  input  in_8,
  input  [31:0] in_9,
  input  [15:0] in_10,
  input  in_11,
  input  in_12,
  input  [31:0] in_13,
  output [31:0] Output
);

  wire and_3_out, and_4_out, and_5_out, and_6_out, and_7_out, C_J_Flag, comparator_1_eq, eq, gtz, L1, L2,
       lez, ltz, neq, not_1_out, not_2_out;
  wire [31:0] Cond_Jump, multiplexer_1_out, PC___Offset, PC_Out;

  // Probe on in_9
  not not_1 (not_1_out, C_J_Flag);
  and and_1 (L1, not_1_out, in_3);
  not not_2 (not_2_out, in_3);
  and and_2 (L2, not_2_out, in_5);
  Adder #(.width(32)) adder_1 (.a(in_1), .b(32'h4), .out(PC_Out));  // open: cin, cout
  Adder #(.width(32)) adder_2 (
    .a(PC_Out), .b({{15{in_10[15]}}, in_10[14:0], 2'b00}), .out(PC___Offset));  // open: cin, cout
  Multiplexer #(.select(2), .width(32), .enable("false")) multiplexer_1 (
    .in0(Cond_Jump), .in1({in_1[31:28], in_2, 2'b00}), .in2(in_9), .out(multiplexer_1_out), .sel({L2, L1}));  // open: in3
  Comparator #(.width(32)) comparator_1 (.a(in_9), .b({32{1'b0}}), .gt(gtz), .eq(comparator_1_eq), .lt(ltz));
  Comparator #(.width(32)) comparator_2 (.a(in_9), .b(in_13), .eq(eq));  // open: gt, lt
  and and_3 (and_3_out, in_11, neq);
  and and_4 (and_4_out, in_4, ltz);
  and and_5 (and_5_out, in_6, gtz);
  and and_6 (and_6_out, in_7, eq);
  and and_7 (and_7_out, in_8, lez);
  Multiplexer #(.width(32), .enable("false")) multiplexer_2 (
    .in0(in_1), .in1(multiplexer_1_out), .out(Output), .sel(in_12));
  or or_1 (lez, comparator_1_eq, ltz);
  not not_3 (neq, eq);
  or or_2 (C_J_Flag, and_3_out, and_4_out, and_5_out, and_6_out, and_7_out);
  Multiplexer #(.width(32), .enable("false")) multiplexer_3 (
    .in0(PC_Out), .in1(PC___Offset), .out(Cond_Jump), .sel(C_J_Flag));

  // Other names for the same wires on the sheet: Offset[15:0] = in_10; A[31:0] = in_9; B[31:0] = in_13; beq = in_7;
  //   bgtz = in_6; blez = in_8; bltz = in_4; bne = in_11; en = in_12; Incond_Jump[31:2] = {in_1[31:28], in_2};
  //   Jump[25:0] = in_2; PC[31:0] = in_1; j = in_3; jr = in_5; Sel[1:0] = {L2, L1}

  // Notes on the sheet:
  //   Flags
endmodule

module InstDecoder (
  input  [31:0] in_1,
  input  in_2,
  output [5:0] OpCode,
  output [25:0] JmpDest,
  output [5:0] FunCode,
  output [4:0] Rs,
  output nTI_TR,
  output [4:0] Rt,
  output [4:0] Rd,
  output [15:0] Constant,
  output add,
  output sltu,
  output sub,
  output mfhi,
  output addi,
  output bne,
  output mul,
  output mflo,
  output andi,
  output blez,
  output mulu,
  output jr,
  output ori,
  output bgtz,
  output div,
  output nop,
  output xori,
  output bltz,
  output divu,
  output pop,
  output slti,
  output lw,
  output \and ,
  output push,
  output sluti,
  output sw,
  output \or ,
  output halt,
  output beq,
  output j,
  output \nor ,
  output tty,
  output \xor ,
  output rnd,
  output slt,
  output kbp
);

  wire addi_t, andi_t, Inm_op, lw_t, ori_t, slti_t, sltiu, xori_t;

  or or_1 (Inm_op, addi_t, ori_t, slti_t, lw_t, andi_t, xori_t, sltiu);
  InstDecoder_TypeR typer_1 (
    .in_1(in_1[31:26]), .in_2(in_1[5:0]), .add(add), .sub(sub), .mul(mul), .mulu(mulu), .div(div),
    .divu(divu), .\and (\and ), .\or (\or ), .\nor (\nor ), .\xor (\xor ), .slt(slt), .sltu(sltu),
    .mfhi(mfhi), .mfllo(mflo), .jr(jr), .nop(nop), .halt(halt), .tty(tty), .pop(pop), .push(push), .rnd(rnd),
    .kbp(kbp), .out_19(nTI_TR));
  InstDecoder_TypeI typei_1 (
    .in_1(in_1[31:26]), .addi(addi), .andi(andi), .ori(ori), .xori(xori), .slti(slti), .sltui(sluti),
    .beq(beq), .bne(bne), .blez(blez), .bgtz(bgtz), .bltz(bltz), .lw(lw), .sw(sw), .addi_2(j));

  assign Constant = in_1[15:0];
  assign FunCode = in_1[5:0];
  assign JmpDest = in_1[25:0];
  assign OpCode = in_1[31:26];
  assign Rd = in_1[15:11];
  assign Rs = in_1[25:21];
  assign Rt = in_1[20:16];

  // Other names for the same wires on the sheet: En = in_2; X[4:0] = in_1[10:6]
endmodule

module TypeR (
  input  [5:0] in_1,
  input  [5:0] in_2,
  output add,
  output sub,
  output mul,
  output mulu,
  output div,
  output divu,
  output \and ,
  output \or ,
  output \nor ,
  output \xor ,
  output slt,
  output sltu,
  output mfhi,
  output mfllo,
  output jr,
  output nop,
  output halt,
  output tty,
  output pop,
  output push,
  output rnd,
  output kbp
);

  wire R1, R2, R3;

  and and_1 (R1, ~in_1[0], ~in_1[1], ~in_1[2], ~in_1[4], ~in_1[4], ~in_1[5]);  // AND_Gate
  and and_2 (R2, ~in_1[0], ~in_1[1], ~in_1[2], in_1[3], in_1[4], in_1[5]);  // AND_Gate
  and and_3 (R3, in_1[0], in_1[1], in_1[2], in_1[3], in_1[4], in_1[5]);
  and and_4 (add, ~in_2[0], ~in_2[1], ~in_2[2], ~in_2[3], ~in_2[4], in_2[5], R1);  // AND_Gate
  and and_5 (divu, in_2[0], in_2[1], ~in_2[2], in_2[3], in_2[4], ~in_2[5], R1);  // AND_Gate
  and and_6 (slt, ~in_2[0], in_2[1], ~in_2[2], in_2[3], ~in_2[4], in_2[5], R1);  // AND_Gate
  and and_7 (nop, ~in_2[0], ~in_2[1], ~in_2[2], ~in_2[3], ~in_2[4], ~in_2[5], R1);  // AND_Gate
  and and_8 (pop, ~in_2[0], ~in_2[1], ~in_2[2], ~in_2[3], ~in_2[4], ~in_2[5], R2);  // AND_Gate
  and and_9 (sub, ~in_2[0], in_2[1], ~in_2[2], ~in_2[3], ~in_2[4], in_2[5], R1);  // AND_Gate
  and and_10 (\and , ~in_2[0], ~in_2[1], in_2[2], ~in_2[3], ~in_2[4], in_2[5], R1);  // AND_Gate
  and and_11 (sltu, in_2[0], in_2[1], ~in_2[2], in_2[3], ~in_2[4], in_2[5], R1);  // AND_Gate
  and and_12 (push, in_2[0], ~in_2[1], ~in_2[2], ~in_2[3], ~in_2[4], ~in_2[5], R2);  // AND_Gate
  and and_13 (mul, ~in_2[0], ~in_2[1], ~in_2[2], in_2[3], in_2[4], ~in_2[5], R1);  // AND_Gate
  and and_14 (\or , in_2[0], ~in_2[1], in_2[2], ~in_2[3], ~in_2[4], in_2[5], R1);  // AND_Gate
  and and_15 (mfhi, ~in_2[0], ~in_2[1], ~in_2[2], ~in_2[3], in_2[4], ~in_2[5], R1);  // AND_Gate
  and and_16 (halt, in_2[0], in_2[1], in_2[2], in_2[3], in_2[4], in_2[5], R3);
  and and_17 (rnd, ~in_2[0], in_2[1], ~in_2[2], ~in_2[3], ~in_2[4], ~in_2[5], R3);  // AND_Gate
  and and_18 (mulu, in_2[0], ~in_2[1], ~in_2[2], in_2[3], in_2[4], ~in_2[5], R1);  // AND_Gate
  and and_19 (\nor , in_2[0], in_2[1], in_2[2], ~in_2[3], ~in_2[4], in_2[5], R1);  // AND_Gate
  and and_20 (mfllo, ~in_2[0], in_2[1], ~in_2[2], ~in_2[3], in_2[4], ~in_2[5], R1);  // AND_Gate
  and and_21 (div, ~in_2[0], in_2[1], ~in_2[2], in_2[3], in_2[4], ~in_2[5], R1);  // AND_Gate
  and and_22 (\xor , ~in_2[0], ~in_2[1], ~in_2[2], in_2[3], ~in_2[4], in_2[5], R1);  // AND_Gate
  and and_23 (jr, ~in_2[0], ~in_2[1], ~in_2[2], in_2[3], ~in_2[4], ~in_2[5], R1);  // AND_Gate
  and and_24 (tty, in_2[0], ~in_2[1], ~in_2[2], ~in_2[3], ~in_2[4], ~in_2[5], R3);  // AND_Gate
  and and_25 (kbp, ~in_2[0], ~in_2[1], in_2[2], ~in_2[3], ~in_2[4], ~in_2[5], R3);  // AND_Gate

  // Other names for the same wires on the sheet: FunCode[5:0] = in_2; OpCode[5:0] = in_1

  // Notes on the sheet:
  //   OPcode 111000
  //   OPcode 000000
  //   OPcode 111111
endmodule

module TypeI (
  input  [5:0] in_1,
  output addi,
  output andi,
  output ori,
  output xori,
  output slti,
  output sltui,
  output beq,
  output bne,
  output blez,
  output bgtz,
  output bltz,
  output lw,
  output sw
);

  and and_1 (addi, ~in_1[0], ~in_1[1], ~in_1[2], in_1[3], ~in_1[4], ~in_1[5]);  // AND_Gate
  and and_2 (sltui, in_1[0], in_1[1], ~in_1[2], in_1[3], ~in_1[4], ~in_1[5]);  // AND_Gate
  and and_3 (bltz, in_1[0], ~in_1[1], ~in_1[2], ~in_1[3], ~in_1[4], ~in_1[5]);  // AND_Gate
  and and_4 (andi, ~in_1[0], ~in_1[1], in_1[2], in_1[3], ~in_1[4], ~in_1[5]);  // AND_Gate
  and and_5 (beq, ~in_1[0], ~in_1[1], in_1[2], ~in_1[3], ~in_1[4], ~in_1[5]);  // AND_Gate
  and and_6 (lw, in_1[0], in_1[1], ~in_1[2], ~in_1[3], ~in_1[4], in_1[5]);  // AND_Gate
  and and_7 (ori, in_1[0], ~in_1[1], in_1[2], in_1[3], ~in_1[4], ~in_1[5]);  // AND_Gate
  and and_8 (bne, in_1[0], ~in_1[1], in_1[2], ~in_1[3], ~in_1[4], ~in_1[5]);  // AND_Gate
  and and_9 (sw, in_1[0], in_1[1], ~in_1[2], in_1[3], ~in_1[4], in_1[5]);  // AND_Gate
  and and_10 (xori, ~in_1[0], in_1[1], in_1[2], in_1[3], ~in_1[4], ~in_1[5]);  // AND_Gate
  and and_11 (blez, ~in_1[0], in_1[1], in_1[2], ~in_1[3], ~in_1[4], ~in_1[5]);  // AND_Gate
  and and_12 (slti, ~in_1[0], in_1[1], ~in_1[2], in_1[3], ~in_1[4], ~in_1[5]);  // AND_Gate
  and and_13 (bgtz, in_1[0], in_1[1], in_1[2], ~in_1[3], ~in_1[4], ~in_1[5]);  // AND_Gate

  // Other names for the same wires on the sheet: OpCode[5:0] = in_1
endmodule

module MemoryReader (
  input  [31:0] in_1,
  input  [31:0] in_2,
  input  [31:0] in_3,
  input  [31:0] in_4,
  input  [31:0] in_5,
  input  in_6,
  input  in_7,
  input  in_8,
  input  [3:0] in_9,
  output [15:0] Address,
  output [3:0] out_11,
  output CS,
  output Reading,
  output [31:0] Instruction,
  output Final
);

  wire demultiplexer_1_out0, demultiplexer_1_out1, demultiplexer_2_out1, or_1_out, or_2_out, or_3_out,
       RST_Count;
  wire [3:0] counter_1_q;
  wire [7:0] Byte_0, Byte_1, Byte_2, Byte_3;

  Multiplexer #(.select(4), .width(32), .enable("false")) multiplexer_1 (
    .in1(in_1), .in2(in_2), .in4(in_3), .in8(in_4), .out({Byte_0, Byte_1, Byte_2, Byte_3}), .sel(out_11));  // open: in0, in3, in5, in6, in7, in9, in10, in11, in12, in13, in14, in15
  or or_1 (or_1_out, demultiplexer_1_out0, demultiplexer_2_out1);
  Shifter #(.width(4)) shifter_1 (.in(4'b0001), .\dist (in_5[3:2]), .out(out_11));
  D_Flip_Flop IDLE (.clk(in_8), .D(or_1_out), .Q(RST_Count), .preset(in_7));  // open: Qn, en, reset
  Demultiplexer #(.enable("false")) demultiplexer_1 (
    .out0(demultiplexer_1_out0), .out1(demultiplexer_1_out1), .in(RST_Count), .sel(in_6));
  Register #(.width(32)) register_1 (
    .D({Byte_3, Byte_2, Byte_1, Byte_0}), .en(Final), .Q(Instruction), .clk(in_8), .clr(in_7));
  D_Flip_Flop COUNT (.clk(in_8), .D(or_2_out), .Q(CS), .reset(in_7));  // open: Qn, preset, en
  or or_2 (or_2_out, demultiplexer_1_out1, Reading);
  Counter #(.width(4), .max('hf)) counter_1 (
    .count(CS), .Q(counter_1_q), .clk(in_8), .clr(or_3_out));  // open: load, D, carry
  or or_3 (or_3_out, RST_Count, in_7);
  Demultiplexer #(.enable("false")) demultiplexer_2 (.out0(Reading), .out1(demultiplexer_2_out1), .in(CS), .sel(Final));
  Comparator #(.width(4)) comparator_1 (.a(counter_1_q), .b(in_9), .eq(Final));  // open: gt, lt

  assign Address = in_5[19:4];

  // Other names for the same wires on the sheet: Address_t[31:0] = in_5; CLK = in_8; Cond = Final; En = in_6;
  //   Inc = CS; Mask[3:0] = out_11; Ram_1[31:0] = in_1; Ram_2[31:0] = in_2; Ram_3[31:0] = in_3; Ram_4[31:0] = in_4;
  //   ReadTime[3:0] = in_9; RST = in_7
endmodule

module MemoryWritter (
  input  [31:0] in_1,
  input  [31:0] in_2,
  input  in_3,
  input  in_4,
  input  in_5,
  input  [3:0] in_6,
  output [31:0] Ram_0,
  output Writting,
  output [3:0] Mask,
  output [31:0] Ram_1,
  output [15:0] Address_Out,
  output CS,
  output [31:0] Ram_2,
  output [31:0] Ram_3,
  output Final
);

  wire demultiplexer_1_out0, demultiplexer_1_out1, demultiplexer_2_out1, or_1_out, or_2_out, or_3_out,
       RST_Count;
  wire [3:0] counter_1_q;

  or or_1 (or_1_out, demultiplexer_1_out0, demultiplexer_2_out1);
  D_Flip_Flop IDLE (.clk(in_3), .D(or_1_out), .Q(RST_Count), .preset(in_4));  // open: Qn, en, reset
  Demultiplexer #(.enable("false")) demultiplexer_1 (
    .out0(demultiplexer_1_out0), .out1(demultiplexer_1_out1), .in(RST_Count), .sel(in_5));
  Counter #(.width(4), .max('hf)) counter_1 (
    .count(CS), .Q(counter_1_q), .clk(in_3), .clr(or_2_out));  // open: load, D, carry
  or or_2 (or_2_out, RST_Count, in_4);
  or or_3 (or_3_out, demultiplexer_1_out1, Writting);
  Demultiplexer #(.enable("false")) demultiplexer_2 (
    .out0(Writting), .out1(demultiplexer_2_out1), .in(CS), .sel(Final));
  D_Flip_Flop COUNT (.clk(in_3), .D(or_3_out), .Q(CS), .reset(in_4));  // open: Qn, preset, en
  Comparator #(.width(4)) comparator_1 (.a(counter_1_q), .b(in_6), .eq(Final));  // open: gt, lt
  Shifter #(.width(4)) shifter_1 (.in(4'b0001), .\dist (in_2[3:2]), .out(Mask));

  assign Address_Out = in_2[19:4];
  assign Ram_0 = {in_1[7:0], in_1[15:8], in_1[23:16], in_1[31:24]};
  assign Ram_1 = {in_1[7:0], in_1[15:8], in_1[23:16], in_1[31:24]};
  assign Ram_2 = {in_1[7:0], in_1[15:8], in_1[23:16], in_1[31:24]};
  assign Ram_3 = {in_1[7:0], in_1[15:8], in_1[23:16], in_1[31:24]};

  // Other names for the same wires on the sheet: Address[31:0] = in_2; CLK = in_3; Cond = Final; En = in_5; Inc = CS;
  //   Byte_3[7:0] = in_1[7:0]; Input[31:0] = in_1; Byte_2[7:0] = in_1[15:8]; Byte_0[7:0] = in_1[31:24];
  //   Byte_1[7:0] = in_1[23:16]; RST = in_4; WriteTime[3:0] = in_6
endmodule

module Op_Decoder (
  input  [5:0] in_1,
  output [3:0] Output
);

  wire and_1_out, and_2_out, and_3_out, and_4_out, and_5_out, and_6_out, and_7_out, and_8_out, and_9_out,
       and_10_out, and_11_out, and_12_out, not_1_out, not_2_out, not_3_out, not_4_out, not_5_out, not_6_out,
       not_7_out, not_8_out, not_9_out, not_10_out, not_11_out, not_12_out, not_13_out, not_14_out,
       not_15_out, not_16_out;

  not not_1 (not_1_out, in_1[3]);
  not not_2 (not_2_out, in_1[0]);
  not not_3 (not_3_out, in_1[4]);
  not not_4 (not_4_out, in_1[3]);
  not not_5 (not_5_out, in_1[1]);
  not not_6 (not_6_out, in_1[5]);
  not not_7 (not_7_out, in_1[2]);
  not not_8 (not_8_out, in_1[1]);
  not not_9 (not_9_out, in_1[0]);
  not not_10 (not_10_out, in_1[2]);
  not not_11 (not_11_out, in_1[1]);
  not not_12 (not_12_out, in_1[0]);
  not not_13 (not_13_out, in_1[0]);
  not not_14 (not_14_out, in_1[0]);
  not not_15 (not_15_out, in_1[4]);
  not not_16 (not_16_out, in_1[0]);
  and and_1 (and_1_out, not_1_out, in_1[1], not_2_out);
  and and_2 (and_2_out, in_1[5], not_3_out, not_4_out, in_1[2], in_1[1]);
  and and_3 (and_3_out, in_1[2], not_5_out, in_1[0]);
  and and_4 (and_4_out, not_6_out, in_1[2], in_1[1]);
  and and_5 (and_5_out, in_1[3], in_1[2], in_1[0]);
  and and_6 (and_6_out, in_1[5], in_1[3], not_7_out, not_8_out, not_9_out);
  and and_7 (and_7_out, not_10_out, in_1[0]);
  and and_8 (and_8_out, in_1[2], not_11_out, not_12_out);
  and and_9 (and_9_out, in_1[2], not_13_out);
  and and_10 (and_10_out, in_1[2], in_1[1]);
  and and_11 (and_11_out, in_1[3], in_1[1], not_14_out);
  and and_12 (and_12_out, in_1[5], not_15_out, in_1[3], not_16_out);
  or or_1 (Output[3], and_1_out, and_2_out);
  or or_2 (Output[2], and_3_out, and_4_out, and_5_out, in_1[4], and_6_out);
  or or_3 (Output[1], and_7_out, and_8_out, in_1[4]);
  or or_4 (Output[0], and_9_out, and_10_out, and_11_out, and_12_out);
endmodule

module Address_Sel (
  input  lw,
  input  pop,
  output o1,
  output o2
);


  assign o1 = pop;
  assign o2 = lw;
endmodule

module DataPath (
  input  [4:0] in_1,
  input  [4:0] RtLo,
  input  [31:0] in_3,
  input  in_4,
  input  in_5,
  input  in_6,
  input  in_7,
  input  in_8,
  input  in_9,
  input  [6:0] in_10,
  input  in_11,
  input  in_12,
  output [31:0] out_13,
  output [31:0] out_14,
  output [31:0] out_15,
  output [6:0] out_16,
  output out_17,
  output [31:0] out_18,
  output [4:0] out_19,
  output out_20,
  output [4:0] out_21,
  output [31:0] out_22,
  output out_23,
  output out_24,
  output out_25,
  output out_26,
  output out_27
);

  wire add, addi, \and , and_2_out, and_7_out, andi, beq, bgtz, blez, bltz, bne, div, divu, Inm_op, j, jr,
       lw, mfHi, mfLo, mul, mulu, NF, nop, \nor , nTI_TR, \or , or_3_out, or_4_out, or_5_out, ori, pop, push,
       rnd, slt, slti, sltiu, sltu, sub, sw, W_in_RT, Write_En, \xor , xori, ZF;
  wire [2:0] multiplexer_9_out, multiplexer_10_out, multiplexer_12_out, multiplexer_13_out, S_IR;
  wire [4:0] multiplexer_2_out, multiplexer_3_out, multiplexer_4_out, RS;
  wire [5:0] FunCode, multiplexer_6_out, OpCode;
  wire [15:0] Constant;
  wire [25:0] JmpDest;
  wire [31:0] ALU_Out, bit_extender_1_out, bit_extender_2_out, Hi, Input_PC, kbd_Input, Lo,
       multiplexer_5_out, multiplexer_7_out, RF_Input, rnd_Value, Value_2;

  or or_1 (Inm_op, addi, ori, slti, lw, andi, xori, sltiu);
  or or_2 (W_in_RT, addi, ori, slti, andi, xori, sltiu, in_12);
  Multiplexer #(.width(32), .enable("false")) multiplexer_1 (
    .in0({32{1'b1}}), .in1({{25{1'b0}}, in_10}), .out(kbd_Input), .sel(in_9));
  or or_3 (or_3_out, add, sub, addi, \and , \nor , \or , \xor , ori, andi, xori, slt, sltu, slti, sltiu, mfHi, mfLo, in_12, in_11, rnd, out_25);
  and and_1 (Write_En, in_6, or_3_out);
  InstDecoder instdecoder_1 (
    .in_1(in_3), .add(add), .sub(sub), .addi(addi), .in_2(in_7), .mul(mul), .andi(andi), .mulu(mulu),
    .ori(ori), .div(div), .xori(xori), .divu(divu), .slti(slti), .\and (\and ), .sluti(sltiu), .\or (\or ),
    .beq(beq), .\nor (\nor ), .\xor (\xor ), .slt(slt), .OpCode(OpCode), .JmpDest(JmpDest),
    .FunCode(FunCode), .Rs(RS), .Rt(out_19), .Rd(out_21), .Constant(Constant), .sltu(sltu), .mfhi(mfHi),
    .bne(bne), .mflo(mfLo), .blez(blez), .jr(jr), .bgtz(bgtz), .nop(nop), .bltz(bltz), .pop(pop), .lw(lw),
    .push(push), .sw(sw), .halt(out_23), .tty(out_26), .rnd(rnd), .kbp(out_25), .nTI_TR(nTI_TR), .j(j));
  Multiplexer #(.width(5), .enable("false")) multiplexer_2 (
    .in0(out_21), .in1(in_1), .out(multiplexer_2_out), .sel(in_11));
  Multiplexer #(.width(5), .enable("false")) multiplexer_3 (
    .in0(multiplexer_2_out), .in1(multiplexer_4_out), .out(multiplexer_3_out), .sel(W_in_RT));
  Multiplexer #(.width(5), .enable("false")) multiplexer_4 (
    .in0(out_19), .in1(RtLo), .out(multiplexer_4_out), .sel(in_12));
  Multiplexer #(.width(32), .enable("false")) multiplexer_5 (
    .in0(Value_2), .in1(out_15), .out(multiplexer_5_out), .sel(Inm_op));
  Multiplexer #(.width(6), .enable("false")) multiplexer_6 (
    .in0(OpCode), .in1(FunCode), .out(multiplexer_6_out), .sel(nTI_TR));
  Random #(.width(32)) random_1 (.clk(in_4), .out(rnd_Value));  // open: next, clr
  RegisterFile registerfile_1 (
    .Input(RF_Input), .RST(in_5), .in_3(in_4), .in_4(Write_En), .in_5(RS), .in_6(out_19),
    .in_7(multiplexer_3_out), .in_8(and_2_out), .in_9(in_11), .SP_Output(out_22), .A(out_14), .B(Value_2));
  and and_2 (and_2_out, push, in_7);
  BranchControlUnit branchcontrolunit_1 (
    .in_1(out_18), .in_2(JmpDest), .in_3(j), .in_4(bltz), .in_5(jr), .in_6(bgtz), .in_7(beq), .in_8(blez),
    .in_9(out_14), .in_10(Constant), .in_11(bne), .in_12(in_8), .in_13(Value_2), .Output(Input_PC));
  ALU alu_1 (
    .A(out_14), .B(multiplexer_5_out), .FuncCode(multiplexer_6_out), .NF(NF), .Result(ALU_Out), .ZF(ZF),
    .Hi(Hi), .Lo(Lo), .in_3(in_4), .in_4(in_5));
  Multiplexer #(.width(32), .enable("false")) multiplexer_7 (
    .in0(out_14), .in1(Value_2), .out(multiplexer_7_out), .sel(sw));
  Multiplexer #(.width(32), .enable("false")) multiplexer_8 (
    .in0(multiplexer_7_out), .in1(out_14), .out(out_13), .sel(in_5));
  Multiplexer #(.width(3), .enable("false")) multiplexer_9 (
    .in0(3'b001), .in1(3'b010), .out(multiplexer_9_out), .sel(mfLo));
  Multiplexer #(.width(3), .enable("false")) multiplexer_10 (
    .in0(3'b000), .in1(multiplexer_9_out), .out(multiplexer_10_out), .sel(or_4_out));
  or or_4 (or_4_out, mfLo, mfHi);
  and and_3 (out_17, in_7, pop);
  and and_4 (out_20, in_7, push);
  and and_5 (out_24, in_7, lw);
  and and_6 (out_27, in_7, sw);
  Multiplexer #(.select(3), .width(32), .enable("false")) multiplexer_11 (
    .in0(ALU_Out), .in1(Hi), .in2(Lo), .in3(rnd_Value), .in4(in_3), .in5(kbd_Input), .out(RF_Input),
    .sel(S_IR));  // open: in6, in7
  Multiplexer #(.width(3), .enable("false")) multiplexer_12 (
    .in0(multiplexer_10_out), .in1(3'b011), .out(multiplexer_12_out), .sel(rnd));
  Multiplexer #(.width(3), .enable("false")) multiplexer_13 (
    .in0(multiplexer_12_out), .in1(3'b100), .out(multiplexer_13_out), .sel(or_5_out));
  or or_5 (or_5_out, in_12, in_11);
  assign bit_extender_1_out = {{16{Constant[15]}}, Constant};  // Bit_Extender bit_extender_1
  Multiplexer #(.width(32), .enable("false")) multiplexer_14 (
    .in0(bit_extender_1_out), .in1(bit_extender_2_out), .out(out_15), .sel(and_7_out));
  assign bit_extender_2_out = {{16{1'b0}}, Constant};  // Bit_Extender bit_extender_2
  and and_7 (and_7_out, in_6, nTI_TR);
  Multiplexer #(.width(3), .enable("false")) multiplexer_15 (
    .in0(multiplexer_13_out), .in1(3'b101), .out(S_IR), .sel(out_25));
  PC pc_1 (.in_1(Input_PC), .in_2(in_8), .in_3(in_4), .in_4(in_5), .Output(out_18));
  // Probe on out_15

  assign out_16 = out_14[6:0];

  // Other names for the same wires on the sheet: CLK = in_4; CLR = in_5; Constant_32b[31:0] = out_15;
  //   Decoder_En = in_7; Final = in_6; halt = out_23; Instruction[31:0] = in_3; kbd = out_25; kbd2[6:0] = in_10;
  //   KBD_DATA[6:0] = in_10; KBD_AVAIL = in_9; lw_En = in_12; PC_En = in_8; PC_Out[31:0] = out_18; Pop_En = in_11;
  //   RAM_Input[31:0] = out_13; RD[4:0] = out_21; RdPop[4:0] = in_1; RT[4:0] = out_19; SP[31:0] = out_22;
  //   tty = out_26; TTY_Data[6:0] = out_14[6:0]; Value_1[31:0] = out_14
endmodule
